// Logisim project OC.circ as structural Verilog: 7 circuits, main circuit somador8bits
module main (
  input  in_1,
  input  [7:0] in_2,
  input  [7:0] in_3,
  input  in_4,
  input  in_5,
  input  in_6,
  input  [7:0] in_7,
  output [7:0] out_8,
  output out_9,
  output out_10,
  output [7:0] out_11
);

  Memoria1Bit memoria1bit_1 (.S(in_5), .I(in_4), .Q(out_10));
  Memoria8Bits memoria8bits_1 (.in_2(in_7), .in_1(in_6), .out_3(out_11));
  Registrador registrador_1 ();  // open: I, S, E, O
  somador8bits somador8bits_1 (.B(in_3), .A(in_2), .in_2(in_1), .S(out_8), .out_4(out_9));
endmodule

module somador1bit (
  input  Cin,
  input  A,
  input  B,
  output S,
  output Cout
);

  wire and_1_out, and_2_out, xor_1_out;

  and and_1 (and_1_out, A, B);
  xor xor_1 (xor_1_out, A, B);
  or or_1 (Cout, and_1_out, and_2_out);
  and and_2 (and_2_out, xor_1_out, Cin);
  xor xor_2 (S, Cin, xor_1_out);
endmodule

module somador8bits (
  input  [7:0] A,
  input  in_2,
  input  [7:0] B,
  output out_4,
  output [7:0] S
);

  wire somador1bit_1_cout, somador1bit_3_cout, somador1bit_4_cout, somador1bit_5_cout, somador1bit_6_cout,
       somador1bit_7_cout;

  somador1bit somador1bit_1 (.A(A[0]), .B(B[0]), .Cin(in_2), .Cout(somador1bit_1_cout), .S(S[0]));
  somador1bit somador1bit_2 (.A(A[1]), .B(B[1]), .Cin(somador1bit_1_cout), .Cout(B[2]), .S(S[1]));
  somador1bit somador1bit_3 (.A(A[2]), .B(B[2]), .Cin(B[2]), .Cout(somador1bit_3_cout), .S(S[2]));
  somador1bit somador1bit_4 (.A(A[3]), .B(B[3]), .Cin(somador1bit_3_cout), .Cout(somador1bit_4_cout), .S(S[3]));
  somador1bit somador1bit_5 (.A(A[4]), .B(B[4]), .Cin(somador1bit_4_cout), .Cout(somador1bit_5_cout), .S(S[4]));
  somador1bit somador1bit_6 (.A(A[5]), .B(B[5]), .Cin(somador1bit_5_cout), .Cout(somador1bit_6_cout), .S(S[5]));
  somador1bit somador1bit_7 (.A(A[6]), .B(B[6]), .Cin(somador1bit_6_cout), .Cout(somador1bit_7_cout), .S(S[6]));
  somador1bit somador1bit_8 (.A(A[7]), .B(B[7]), .Cin(somador1bit_7_cout), .Cout(out_4), .S(S[7]));
endmodule

module Memoria1Bit (
  input  I,
  input  S,
  output Q
);

  wire nand_1_out, nand_2_out, nand_4_out;

  nand nand_1 (nand_1_out, I, S);
  nand nand_2 (nand_2_out, nand_1_out, S);
  nand nand_3 (Q, nand_1_out, nand_4_out);
  nand nand_4 (nand_4_out, Q, nand_2_out);

  // Notes on the sheet:
  //   Input | Set | Output
  //   0   |  0  |  x
  //   1   |  0  |  x
  //   0   |  1  |  0
  //   1   |  1  |  1
  //   (armazenado)
  //   (armazenado)
endmodule

module Memoria8Bits (
  input  in_1,
  input  [7:0] in_2,
  output [7:0] out_3
);

  Memoria1Bit memoria1bit_1 (.S(in_1), .I(in_2[0]), .Q(out_3[0]));
  Memoria1Bit memoria1bit_2 (.S(in_1), .I(in_2[1]), .Q(out_3[1]));
  Memoria1Bit memoria1bit_3 (.S(in_1), .I(in_2[2]), .Q(out_3[2]));
  Memoria1Bit memoria1bit_4 (.S(in_1), .I(in_2[3]), .Q(out_3[3]));
  Memoria1Bit memoria1bit_5 (.S(in_1), .I(in_2[4]), .Q(out_3[4]));
  Memoria1Bit memoria1bit_6 (.S(in_1), .I(in_2[5]), .Q(out_3[5]));
  Memoria1Bit memoria1bit_7 (.S(in_1), .I(in_2[6]), .Q(out_3[6]));
  Memoria1Bit memoria1bit_8 (.S(in_1), .I(in_2[7]), .Q(out_3[7]));
endmodule

module Registrador (
  input  S,
  input  [7:0] I,
  input  E,
  output [7:0] O
);

  wire [7:0] memoria8bits_1_out_3;

  Memoria8Bits memoria8bits_1 (.in_2(I), .in_1(S), .out_3(memoria8bits_1_out_3));
  and and_1 (O[0], memoria8bits_1_out_3[0], E);
  and and_2 (O[1], memoria8bits_1_out_3[1], E);
  and and_3 (O[2], memoria8bits_1_out_3[2], E);
  and and_4 (O[3], memoria8bits_1_out_3[3], E);
  and and_5 (O[4], memoria8bits_1_out_3[4], E);
  and and_6 (O[5], memoria8bits_1_out_3[5], E);
  and and_7 (O[6], memoria8bits_1_out_3[6], E);
  and and_8 (O[7], memoria8bits_1_out_3[7], E);
endmodule

module Memoria1byte (
  input  Set,
  input  [7:0] Inp,
  output out_3,
  output out_4,
  output out_5,
  output out_6,
  output out_7,
  output out_8,
  output out_9,
  output out_10
);

  Memoria1Bit memoria1bit_1 (.S(Set), .I(Inp[0]), .Q(out_3));
  Memoria1Bit memoria1bit_2 (.S(Set), .I(Inp[1]), .Q(out_4));
  Memoria1Bit memoria1bit_3 (.S(Set), .I(Inp[2]), .Q(out_5));
  Memoria1Bit memoria1bit_4 (.S(Set), .I(Inp[3]), .Q(out_6));
  Memoria1Bit memoria1bit_5 (.S(Set), .I(Inp[4]), .Q(out_7));
  Memoria1Bit memoria1bit_6 (.S(Set), .I(Inp[5]), .Q(out_8));
  Memoria1Bit memoria1bit_7 (.S(Set), .I(Inp[6]), .Q(out_9));
  Memoria1Bit memoria1bit_8 (.S(Set), .I(Inp[7]), .Q(out_10));
endmodule
